# Fritzing sketch CDB (saved by Fritzing 1.0.5)

parts:
  J1 = Piezo Speaker
  M3 = RioRand LM2596
  RFM95W1 = RFM95W LoRa Module
  J2 = Basic Servo
  A2 = Esp32-c3 super mini
  M4 = NEO-6M GPS Module [part_number=GY-GPS6MV2]
  A3 = GY-BMP280 Breakout
  Componente1 = InvenSense MPU6050

nets:
  GND: J1.pin1, M3.Pin_4, RFM95W1.8_GND, RFM95W1.10_GND, RFM95W1.11_DIO3, J2.gnd, M4.GND, A3.Pin_2, Componente1.GND
  N1: J1.pin2, A2.Pin_9
  VCC: M3.Pin_3, RFM95W1.13_3.3V, J2.vcc, A2.Pin_14, M4.Vcc, A3.Pin_1, Componente1.VCC
  N2: RFM95W1.2_MISO, A2.Pin_1
  N3: RFM95W1.3_MOSI, A2.Pin_2
  N4: RFM95W1.4_SCK, A2.Pin_13
  N5: RFM95W1.5_NSS_(CS), A2.Pin_3
  N6: RFM95W1.6_RESET, A2.Pin_10
  N7: RFM95W1.14_DIO0, A2.Pin_11
  N8: J2.pulse, A2.Pin_6
  N9: A2.Pin_4, A3.Pin_4, Componente1.SDA
  N10: A2.Pin_5, A3.Pin_3, Componente1.SCL
  N11: A2.Pin_7, M4.Tx
  N12: A2.Pin_8, M4.Rx

custom parts:
  RFM95W LoRa Module: RF Transceiver by Hope RF. Well supported Arduino libraries are available. This Low Power Long Range Transceiver Module for the frequencies 868MHz and 915MHz and it is also available in other versions. This particular part is set for trhough hole rather than SMD in pcb view.
  Esp32-c3 super mini: ESP32-C3 Development Board ESP32 SuperMini Development Board ESP32 Development Board WiFi Bluetooth.
  NEO-6M GPS Module: GY-GPS6MV2 NEO-6M GPS Module Module based on U-blox NEO-6M GPS engine, incorporating regulator for 3.3-5V DC input, MS621FE-compatible rechargeable battery for backup and EEPROM for storing configuration settings. Links: NEO-6 series product information page NEO-6 Datasheet
